// Logisim project niiio.circ as structural Verilog: 7 circuits, main circuit main
module main (
  input  in_1
);

  wire rest, sp, start;
  wire [1:0] _1, _2;
  wire [3:0] sos_1_out_22, sos_1_out_22_2;
  wire [7:0] sos_1_out_23;
  wire [31:0] sos_1_out_7, sos_1_out_8, sos_1_out_9, sos_1_out_10, sos_1_out_11, sos_1_out_12, sos_1_out_13,
       sos_1_out_14, sos_1_out_15, sos_1_out_16, sos_1_out_17, sos_1_out_18, sos_1_out_19, sos_1_out_20,
       sos_1_out_21;

  Button button_1 (.out(sp));
  Joystick #(.bits(2)) joystick_1 (.x(_1), .y(_2));
  Button button_2 (.out(start));
  Button button_3 (.out(rest));
  DotMatrix #(.matrixcols(15), .matrixrows(32)) dotmatrix_1 (
    .col0(sos_1_out_21), .col1(sos_1_out_20), .col2(sos_1_out_19), .col3(sos_1_out_18), .col4(sos_1_out_17),
    .col5(sos_1_out_16), .col6(sos_1_out_15), .col7(sos_1_out_14), .col8(sos_1_out_13), .col9(sos_1_out_12),
    .col10(sos_1_out_11), .col11(sos_1_out_10), .col12(sos_1_out_9), .col13(sos_1_out_8), .col14(sos_1_out_7));
  sos sos_1 (
    .in_1(sp), .in_2(start), .in_3(rest), .out_22({sos_1_out_22_2, sos_1_out_22}), .out_23(sos_1_out_23),
    .in_4(in_1), .in_5(_1), .in_6(_2), .out_7(sos_1_out_7), .out_8(sos_1_out_8), .out_9(sos_1_out_9),
    .out_10(sos_1_out_10), .out_11(sos_1_out_11), .out_12(sos_1_out_12), .out_13(sos_1_out_13),
    .out_14(sos_1_out_14), .out_15(sos_1_out_15), .out_16(sos_1_out_16), .out_17(sos_1_out_17),
    .out_18(sos_1_out_18), .out_19(sos_1_out_19), .out_20(sos_1_out_20), .out_21(sos_1_out_21));  // open: out_24
  Hex_Digit_Display hex_digit_display_1 (.value(sos_1_out_22_2));  // open: dp
  Hex_Digit_Display hex_digit_display_2 (.value(sos_1_out_22));  // open: dp
  Hex_Digit_Display hex_digit_display_3 (.value(sos_1_out_23[3:0]));  // open: dp
  Hex_Digit_Display hex_digit_display_4 (.value(sos_1_out_23[7:4]));  // open: dp
endmodule

module sos (
  input  in_1,
  input  in_2,
  input  in_3,
  input  in_4,
  input  [1:0] in_5,
  input  [1:0] in_6,
  output [31:0] out_7,
  output [31:0] out_8,
  output [31:0] out_9,
  output [31:0] out_10,
  output [31:0] out_11,
  output [31:0] out_12,
  output [31:0] out_13,
  output [31:0] out_14,
  output [31:0] out_15,
  output [31:0] out_16,
  output [31:0] out_17,
  output [31:0] out_18,
  output [31:0] out_19,
  output [31:0] out_20,
  output [31:0] out_21,
  output [7:0] out_22,
  output [7:0] out_23,
  output out_24
);

  wire button_1_out, button_2_out, register_1_q;
  wire [1:0] _1, _1a, _2, _2a;
  wire [31:0] n1_1_out_7, n1_1_out_8, n1_1_out_9, n1_1_out_10, n1_1_out_11, n1_1_out_12, n1_1_out_13,
       n1_1_out_14, n1_1_out_15, n1_1_out_16, n1_1_out_17;

  Button button_1 (.out(button_1_out));
  Button button_2 (.out(button_2_out));
  Joystick #(.bits(2)) joystick_1 (.x(_1a), .y(_2a));
  Register #(.width(1)) register_1 (
    .D(button_1_out), .Q(register_1_q), .clk(button_1_out), .clr(button_2_out));  // open: en
  Multiplexer #(.width(2), .enable("false")) multiplexer_1 (.in0(in_5), .in1(_1a), .out(_1), .sel(register_1_q));
  Multiplexer #(.width(2), .enable("false")) multiplexer_2 (.in0(in_6), .in1(_2a), .out(_2), .sel(register_1_q));
  DotMatrix #(.matrixcols(15), .matrixrows(32)) dotmatrix_1 (
    .col0(out_21), .col1(out_20), .col2(out_19), .col3(out_18), .col4(out_17), .col5(out_16), .col6(out_15),
    .col7(out_14), .col8(out_13), .col9(out_12), .col10(out_11), .col11(out_10), .col12(out_9),
    .col13(out_8), .col14(out_7));
  bol bol_1 (
    .in_4(n1_1_out_17), .in_6(n1_1_out_16), .in_7(out_23), .in_8(n1_1_out_15), .in_9(n1_1_out_14),
    .in_10(n1_1_out_13), .in_11(n1_1_out_12), .in_12(n1_1_out_11), .in_13(n1_1_out_10), .in_14(n1_1_out_9),
    .in_15(n1_1_out_8), .in_16(n1_1_out_7), .out_18(out_19), .out_19(out_18), .out_20(out_17),
    .out_21(out_16), .out_22(out_15), .out_23(out_14), .out_24(out_13), .out_25(out_12), .out_26(out_11),
    .out_27(out_10), .out_28(out_9), ._0(in_3), .start(in_1), .out_17(out_24), .in_5(out_22), .in_3(in_4));
  _1 u_1_1 (
    .in_3(_1), .in_4(_2), .in_1(in_2), .in_2(in_3), .out_19(out_21), .out_18(out_20), .out_17(n1_1_out_17),
    .out_16(n1_1_out_16), .out_15(n1_1_out_15), .out_14(n1_1_out_14), .out_13(n1_1_out_13),
    .out_12(n1_1_out_12), .out_11(n1_1_out_11), .out_10(n1_1_out_10), .out_9(n1_1_out_9), .out_8(n1_1_out_8),
    .out_7(n1_1_out_7), .out_6(out_8), .out_5(out_7), .out_21(out_23), .out_20(out_22));
  Hex_Digit_Display hex_digit_display_1 (.value(out_22[7:4]));  // open: dp
  Hex_Digit_Display hex_digit_display_2 (.value(out_22[3:0]));  // open: dp
  Hex_Digit_Display hex_digit_display_3 (.value(out_23[7:4]));  // open: dp
  Hex_Digit_Display hex_digit_display_4 (.value(out_23[3:0]));  // open: dp

  // Other names for the same wires on the sheet: rest = in_3; sp = in_1; start = in_2
endmodule

module bol (
  input  start,
  input  _0,
  input  in_3,
  input  [31:0] in_4,
  input  [7:0] in_5,
  input  [31:0] in_6,
  input  [7:0] in_7,
  input  [31:0] in_8,
  input  [31:0] in_9,
  input  [31:0] in_10,
  input  [31:0] in_11,
  input  [31:0] in_12,
  input  [31:0] in_13,
  input  [31:0] in_14,
  input  [31:0] in_15,
  input  [31:0] in_16,
  output out_17,
  output [31:0] out_18,
  output [31:0] out_19,
  output [31:0] out_20,
  output [31:0] out_21,
  output [31:0] out_22,
  output [31:0] out_23,
  output [31:0] out_24,
  output [31:0] out_25,
  output [31:0] out_26,
  output [31:0] out_27,
  output [31:0] out_28
);

  wire _1, clock_1_out, decoder_1_out0, decoder_1_out1, decoder_1_out2, decoder_1_out3, decoder_1_out4,
       decoder_1_out5, decoder_1_out6, decoder_1_out7, decoder_1_out8, decoder_1_out9, decoder_1_out10,
       or_1_out, or_2_out, or_3_out, or_4_out, register_1_q, sos;
  wire [3:0] bit_extender_2_out;
  wire [4:0] bit_extender_1_out;
  wire [31:0] adder_1_out, adder_2_out, adder_3_out, adder_4_out, adder_5_out, adder_6_out, adder_7_out,
       adder_8_out, adder_9_out, adder_10_out, adder_11_out, multiplexer_1_out, shift_register_1_q31;

  Bit_Extender #(.out_width(5)) bit_extender_1 (.in(in_5), .out(bit_extender_1_out));
  Multiplexer #(.select(5), .width(32), .enable("false")) multiplexer_1 (
    .in4(32'h8000000), .in5(32'h4000000), .in6(32'h2000000), .in7(32'h1000000), .in8(32'h800000),
    .in9(32'h400000), .in10(32'h200000), .in11(32'h100000), .in12(32'h80000), .in13(32'h40000),
    .in14(32'h20000), .in15(32'h10000), .in16(32'h8000), .in17(32'h4000), .in18(32'h2000), .in19(32'h1000),
    .in20(32'h800), .in21(32'h400), .in22(32'h200), .in23(32'h100), .out(multiplexer_1_out),
    .sel(bit_extender_1_out));  // open: in0, in1, in2, in3, in24, in25, in26, in27, in28, in29, in30, in31
  Button button_1 ();  // open: out
  or or_1 (or_1_out, sos, start);
  Shift_Register #(.length(32)) shift_register_1 (
    .shift(1'b1), .in(1'b0), .clk(or_1_out), .out(_1), .load(start), .clr(or_2_out),
    .d0(multiplexer_1_out[31]), .q0(shift_register_1_q31[31]), .d1(multiplexer_1_out[30]),
    .q1(shift_register_1_q31[30]), .d2(multiplexer_1_out[29]), .q2(shift_register_1_q31[29]),
    .d3(multiplexer_1_out[28]), .q3(shift_register_1_q31[28]), .d4(multiplexer_1_out[27]),
    .q4(shift_register_1_q31[27]), .d5(multiplexer_1_out[26]), .q5(shift_register_1_q31[26]),
    .d6(multiplexer_1_out[25]), .q6(shift_register_1_q31[25]), .d7(multiplexer_1_out[24]),
    .q7(shift_register_1_q31[24]), .d8(multiplexer_1_out[23]), .q8(shift_register_1_q31[23]),
    .d9(multiplexer_1_out[22]), .q9(shift_register_1_q31[22]), .d10(multiplexer_1_out[21]),
    .q10(shift_register_1_q31[21]), .d11(multiplexer_1_out[20]), .q11(shift_register_1_q31[20]),
    .d12(multiplexer_1_out[19]), .q12(shift_register_1_q31[19]), .d13(multiplexer_1_out[18]),
    .q13(shift_register_1_q31[18]), .d14(multiplexer_1_out[17]), .q14(shift_register_1_q31[17]),
    .d15(multiplexer_1_out[16]), .q15(shift_register_1_q31[16]), .d16(multiplexer_1_out[15]),
    .q16(shift_register_1_q31[15]), .d17(multiplexer_1_out[14]), .q17(shift_register_1_q31[14]),
    .d18(multiplexer_1_out[13]), .q18(shift_register_1_q31[13]), .d19(multiplexer_1_out[12]),
    .q19(shift_register_1_q31[12]), .d20(multiplexer_1_out[11]), .q20(shift_register_1_q31[11]),
    .d21(multiplexer_1_out[10]), .q21(shift_register_1_q31[10]), .d22(multiplexer_1_out[9]),
    .q22(shift_register_1_q31[9]), .d23(multiplexer_1_out[8]), .q23(shift_register_1_q31[8]),
    .d24(multiplexer_1_out[7]), .q24(shift_register_1_q31[7]), .d25(multiplexer_1_out[6]),
    .q25(shift_register_1_q31[6]), .d26(multiplexer_1_out[5]), .q26(shift_register_1_q31[5]),
    .d27(multiplexer_1_out[4]), .q27(shift_register_1_q31[4]), .d28(multiplexer_1_out[3]),
    .q28(shift_register_1_q31[3]), .d29(multiplexer_1_out[2]), .q29(shift_register_1_q31[2]),
    .d30(multiplexer_1_out[1]), .q30(shift_register_1_q31[1]), .d31(multiplexer_1_out[0]),
    .q31(shift_register_1_q31[0]));
  or or_2 (or_2_out, _0, _1);
  Register #(.width(1)) register_1 (.D(start), .Q(register_1_q), .clk(start), .clr(or_3_out));  // open: en
  or or_3 (or_3_out, _0, _1);
  Adder #(.width(32)) adder_1 (.a(in_4), .b(shift_register_1_q31), .out(adder_1_out));  // open: cin, cout
  Adder #(.width(32)) adder_2 (.a(in_6), .b(shift_register_1_q31), .out(adder_2_out));  // open: cin, cout
  Adder #(.width(32)) adder_3 (.a(in_8), .b(shift_register_1_q31), .out(adder_3_out));  // open: cin, cout
  Adder #(.width(32)) adder_4 (.a(in_9), .b(shift_register_1_q31), .out(adder_4_out));  // open: cin, cout
  Adder #(.width(32)) adder_5 (.a(in_10), .b(shift_register_1_q31), .out(adder_5_out));  // open: cin, cout
  Adder #(.width(32)) adder_6 (.a(in_11), .b(shift_register_1_q31), .out(adder_6_out));  // open: cin, cout
  Adder #(.width(32)) adder_7 (.a(in_12), .b(shift_register_1_q31), .out(adder_7_out));  // open: cin, cout
  Adder #(.width(32)) adder_8 (.a(in_13), .b(shift_register_1_q31), .out(adder_8_out));  // open: cin, cout
  Adder #(.width(32)) adder_9 (.a(in_14), .b(shift_register_1_q31), .out(adder_9_out));  // open: cin, cout
  Adder #(.width(32)) adder_10 (.a(in_15), .b(shift_register_1_q31), .out(adder_10_out));  // open: cin, cout
  Adder #(.width(32)) adder_11 (.a(in_16), .b(shift_register_1_q31), .out(adder_11_out));  // open: cin, cout
  and and_1 (sos, register_1_q, clock_1_out);
  Clock clock_1 (.out(clock_1_out));
  Register #(.width(1)) register_2 (.D(_1), .Q(out_17), .clk(_1), .clr(or_4_out));  // open: en
  or or_4 (or_4_out, _0, in_3, start);
  Multiplexer #(.width(32), .enable("false")) multiplexer_2 (
    .in0(in_4), .in1(adder_1_out), .out(out_18), .sel(decoder_1_out0));
  Multiplexer #(.width(32), .enable("false")) multiplexer_3 (
    .in0(in_6), .in1(adder_2_out), .out(out_19), .sel(decoder_1_out1));
  Multiplexer #(.width(32), .enable("false")) multiplexer_4 (
    .in0(in_8), .in1(adder_3_out), .out(out_20), .sel(decoder_1_out2));
  Multiplexer #(.width(32), .enable("false")) multiplexer_5 (
    .in0(in_9), .in1(adder_4_out), .out(out_21), .sel(decoder_1_out3));
  Multiplexer #(.width(32), .enable("false")) multiplexer_6 (
    .in0(in_10), .in1(adder_5_out), .out(out_22), .sel(decoder_1_out4));
  Multiplexer #(.width(32), .enable("false")) multiplexer_7 (
    .in0(in_11), .in1(adder_6_out), .out(out_23), .sel(decoder_1_out5));
  Multiplexer #(.width(32), .enable("false")) multiplexer_8 (
    .in0(in_12), .in1(adder_7_out), .out(out_24), .sel(decoder_1_out6));
  Multiplexer #(.width(32), .enable("false")) multiplexer_9 (
    .in0(in_13), .in1(adder_8_out), .out(out_25), .sel(decoder_1_out7));
  Multiplexer #(.width(32), .enable("false")) multiplexer_10 (
    .in0(in_14), .in1(adder_9_out), .out(out_26), .sel(decoder_1_out8));
  Multiplexer #(.width(32), .enable("false")) multiplexer_11 (
    .in0(in_15), .in1(adder_10_out), .out(out_27), .sel(decoder_1_out9));
  Multiplexer #(.width(32), .enable("false")) multiplexer_12 (
    .in0(in_16), .in1(adder_11_out), .out(out_28), .sel(decoder_1_out10));
  DotMatrix #(.matrixcols(3), .matrixrows(32)) dotmatrix_1 (.col1(out_18));  // open: col0, col2
  Decoder #(.select(4), .enable("false")) decoder_1 (
    .out0(decoder_1_out0), .out1(decoder_1_out1), .out2(decoder_1_out2), .out3(decoder_1_out3),
    .out4(decoder_1_out4), .out5(decoder_1_out5), .out6(decoder_1_out6), .out7(decoder_1_out7),
    .out8(decoder_1_out8), .out9(decoder_1_out9), .out10(decoder_1_out10), .sel(bit_extender_2_out));  // open: out11, out12, out13, out14, out15
  Bit_Extender #(.out_width(4)) bit_extender_2 (.in(in_7), .out(bit_extender_2_out));

  // Other names for the same wires on the sheet: s = start
endmodule

module _1 (
  input  in_1,
  input  in_2,
  input  [1:0] in_3,
  input  [1:0] in_4,
  output [31:0] out_5,
  output [31:0] out_6,
  output [31:0] out_7,
  output [31:0] out_8,
  output [31:0] out_9,
  output [31:0] out_10,
  output [31:0] out_11,
  output [31:0] out_12,
  output [31:0] out_13,
  output [31:0] out_14,
  output [31:0] out_15,
  output [31:0] out_16,
  output [31:0] out_17,
  output [31:0] out_18,
  output [31:0] out_19,
  output [7:0] out_20,
  output [7:0] out_21
);

  wire and_1_out, and_2_out, and_3_out, and_4_out, and_5_out, and_6_out, and_7_out, and_8_out,
       comparator_1_eq, comparator_2_lt, comparator_3_eq, comparator_4_lt, d, m, not_1_out, not_2_out,
       not_3_out, not_4_out, or_1_out, or_2_out, or_3_out, or_4_out, or_5_out, or_6_out, or_7_out, or_8_out,
       or_9_out, or_10_out, register_1_q, tunnel, tunnel_t;
  wire [31:0] n2_1_out_6, n2_2_out_6, n2_3_out_6, n2_4_out_6, n2_5_out_6, n3_1_out_10, n3_1_out_11,
       n3_1_out_12, n3_1_out_13, n3_1_out_14, n3_1_out_15, n3_1_out_16, n3_1_out_17, n3_1_out_18,
       n3_1_out_19, n3_1_out_20, n3_1_out_21, n3_1_out_22, n3_1_out_23, n3_1_out_24;

  or or_1 (or_1_out, tunnel_t, tunnel);
  _2 u_2_1 (.in_1(32'hc), .in_2(tunnel_t), .out_6(n2_1_out_6), .in_4(or_1_out), .in_3(in_2), .in_5(in_1));
  _2 u_2_2 (.in_1(32'he), .in_2(tunnel_t), .out_6(n2_2_out_6), .in_4(or_1_out), .in_3(in_2), .in_5(in_1));
  _2 u_2_3 (.in_1(32'hf), .in_2(tunnel_t), .out_6(n2_3_out_6), .in_4(or_1_out), .in_3(in_2), .in_5(in_1));
  _2 u_2_4 (.in_1(32'he), .in_2(tunnel_t), .out_6(n2_4_out_6), .in_4(or_1_out), .in_3(in_2), .in_5(in_1));
  _2 u_2_5 (.in_1(32'hc), .in_2(tunnel_t), .out_6(n2_5_out_6), .in_4(or_1_out), .in_3(in_2), .in_5(in_1));
  j j_1 (.out_3(tunnel_t), .in_2(in_3), .out_4(tunnel), .in_1(in_4), .out_5(m), .out_6(d));
  Register #(.width(1)) register_1 (.D(in_2), .Q(register_1_q), .clk(in_2), .clr(in_1));  // open: en
  _3 u_3_1 (
    .in_1(n2_1_out_6), .in_2(n2_2_out_6), .in_3(n2_3_out_6), .in_4(n2_4_out_6), .in_5(n2_5_out_6), .in_6(m),
    .out_10(n3_1_out_10), .out_11(n3_1_out_11), .out_12(n3_1_out_12), .out_13(n3_1_out_13),
    .out_14(n3_1_out_14), .out_15(n3_1_out_15), .out_16(n3_1_out_16), .out_17(n3_1_out_17),
    .out_18(n3_1_out_18), .out_19(n3_1_out_19), .out_20(n3_1_out_20), .out_21(n3_1_out_21),
    .out_22(n3_1_out_22), .out_23(n3_1_out_23), .out_24(n3_1_out_24), .in_8(or_2_out), .in_7(in_2),
    .in_9(in_1));
  or or_2 (or_2_out, m, d);
  Multiplexer #(.width(32), .enable("false")) multiplexer_1 (
    .in0(n3_1_out_10), .in1({32{1'b0}}), .out(out_19), .sel(register_1_q));
  Multiplexer #(.width(32), .enable("false")) multiplexer_2 (
    .in0(n3_1_out_11), .in1({32{1'b0}}), .out(out_18), .sel(register_1_q));
  Multiplexer #(.width(32), .enable("false")) multiplexer_3 (
    .in0(n3_1_out_12), .in1({32{1'b0}}), .out(out_17), .sel(register_1_q));
  Multiplexer #(.width(32), .enable("false")) multiplexer_4 (
    .in0(n3_1_out_13), .in1({32{1'b0}}), .out(out_16), .sel(register_1_q));
  Multiplexer #(.width(32), .enable("false")) multiplexer_5 (
    .in0(n3_1_out_14), .in1({32{1'b0}}), .out(out_15), .sel(register_1_q));
  Multiplexer #(.width(32), .enable("false")) multiplexer_6 (
    .in0(n3_1_out_15), .in1({32{1'b0}}), .out(out_14), .sel(register_1_q));
  Multiplexer #(.width(32), .enable("false")) multiplexer_7 (
    .in0(n3_1_out_16), .in1({32{1'b0}}), .out(out_13), .sel(register_1_q));
  Multiplexer #(.width(32), .enable("false")) multiplexer_8 (
    .in0(n3_1_out_17), .in1({32{1'b0}}), .out(out_12), .sel(register_1_q));
  Multiplexer #(.width(32), .enable("false")) multiplexer_9 (
    .in0(n3_1_out_18), .in1({32{1'b0}}), .out(out_11), .sel(register_1_q));
  Multiplexer #(.width(32), .enable("false")) multiplexer_10 (
    .in0(n3_1_out_19), .in1({32{1'b0}}), .out(out_10), .sel(register_1_q));
  Multiplexer #(.width(32), .enable("false")) multiplexer_11 (
    .in0(n3_1_out_20), .in1({32{1'b0}}), .out(out_9), .sel(register_1_q));
  Multiplexer #(.width(32), .enable("false")) multiplexer_12 (
    .in0(n3_1_out_21), .in1({32{1'b0}}), .out(out_8), .sel(register_1_q));
  Multiplexer #(.width(32), .enable("false")) multiplexer_13 (
    .in0(n3_1_out_22), .in1({32{1'b0}}), .out(out_7), .sel(register_1_q));
  Multiplexer #(.width(32), .enable("false")) multiplexer_14 (
    .in0(n3_1_out_23), .in1({32{1'b0}}), .out(out_6), .sel(register_1_q));
  Multiplexer #(.width(32), .enable("false")) multiplexer_15 (
    .in0(n3_1_out_24), .in1({32{1'b0}}), .out(out_5), .sel(register_1_q));
  or or_3 (or_3_out, in_1, and_7_out);
  or or_4 (or_4_out, in_1, tunnel_t);
  Counter counter_1 (
    .load(or_4_out), .D(8'h9), .count(not_1_out), .Q(out_20), .clk(or_5_out), .clr(in_2));  // open: carry
  not not_1 (not_1_out, in_1);
  or or_5 (or_5_out, in_1, and_8_out);
  or or_6 (or_6_out, in_1, m);
  Counter counter_2 (
    .load(or_6_out), .D(8'h5), .count(not_2_out), .Q(out_21), .clk(or_3_out), .clr(in_2));  // open: carry
  not not_2 (not_2_out, in_1);
  Comparator comparator_1 (.a(out_20), .b(8'h3), .eq(comparator_1_eq));  // open: gt, lt
  Comparator comparator_2 (.a(out_20), .b(8'h13), .lt(comparator_2_lt));  // open: gt, eq
  or or_7 (or_7_out, tunnel, tunnel_t);
  and and_1 (and_1_out, tunnel_t, or_7_out);
  Comparator comparator_3 (.a(out_21), .b({8{1'b1}}), .eq(comparator_3_eq));  // open: gt, lt
  Comparator comparator_4 (.a(out_21), .b(8'ha), .lt(comparator_4_lt));  // open: gt, eq
  or or_8 (or_8_out, m, d);
  and and_2 (and_2_out, m, or_8_out);
  and and_3 (and_3_out, comparator_1_eq, tunnel_t);
  not not_3 (not_3_out, and_3_out);
  and and_4 (and_4_out, or_7_out, comparator_2_lt);
  and and_5 (and_5_out, comparator_3_eq, m);
  not not_4 (not_4_out, and_5_out);
  and and_6 (and_6_out, or_8_out, comparator_4_lt);
  or or_9 (or_9_out, and_4_out, and_1_out);
  and and_7 (and_7_out, not_4_out, or_10_out);
  or or_10 (or_10_out, and_6_out, and_2_out);
  and and_8 (and_8_out, not_3_out, or_9_out);

  // Other names for the same wires on the sheet: _1[1:0] = in_3; _2[1:0] = in_4; rest = in_2; start = in_1
endmodule

module j (
  input  [1:0] in_1,
  input  [1:0] in_2,
  output out_3,
  output out_4,
  output out_5,
  output out_6
);

  wire not_1_out, not_2_out;

  and and_1 (out_3, in_1[0], not_1_out);
  not not_1 (not_1_out, in_1[1]);
  and and_2 (out_5, not_2_out, in_2[0]);
  not not_2 (not_2_out, in_2[1]);
  and and_3 (out_6, in_2[1], in_2[0]);
  and and_4 (out_4, in_1[0], in_1[1]);
endmodule

module _2 (
  input  [31:0] in_1,
  input  in_2,
  input  in_3,
  input  in_4,
  input  in_5,
  output [31:0] out_6
);

  wire and_1_out, and_2_out, and_3_out, and_4_out, ckolk, comparator_1_eq, comparator_2_lt, not_1_out,
       not_2_out, or_1_out, or_2_out;
  wire [3:0] bit_extender_1_out;
  wire [4:0] counter_1_q;
  wire [31:0] multiplier_1_out, multiplier_2_out, multiplier_3_out, multiplier_4_out, multiplier_5_out,
       multiplier_6_out, multiplier_7_out, multiplier_8_out, multiplier_9_out, multiplier_10_out,
       multiplier_11_out, multiplier_12_out, multiplier_13_out, multiplier_14_out, multiplier_15_out,
       multiplier_16_out;

  Multiplier #(.width(32)) multiplier_1 (.a(in_1), .b(32'h10000000), .out(multiplier_1_out));  // open: cin, cout
  Multiplier #(.width(32)) multiplier_2 (.a(in_1), .b(32'h8000000), .out(multiplier_2_out));  // open: cin, cout
  Multiplier #(.width(32)) multiplier_3 (.a(in_1), .b(32'h4000000), .out(multiplier_3_out));  // open: cin, cout
  Multiplier #(.width(32)) multiplier_4 (.a(in_1), .b(32'h2000000), .out(multiplier_4_out));  // open: cin, cout
  Multiplier #(.width(32)) multiplier_5 (.a(in_1), .b(32'h1000000), .out(multiplier_5_out));  // open: cin, cout
  Multiplier #(.width(32)) multiplier_6 (.a(in_1), .b(32'h800000), .out(multiplier_6_out));  // open: cin, cout
  Multiplier #(.width(32)) multiplier_7 (.a(in_1), .b(32'h400000), .out(multiplier_7_out));  // open: cin, cout
  Multiplier #(.width(32)) multiplier_8 (.a(in_1), .b(32'h200000), .out(multiplier_8_out));  // open: cin, cout
  Multiplier #(.width(32)) multiplier_9 (.a(in_1), .b(32'h100000), .out(multiplier_9_out));  // open: cin, cout
  Multiplier #(.width(32)) multiplier_10 (.a(in_1), .b(32'h80000), .out(multiplier_10_out));  // open: cin, cout
  Multiplier #(.width(32)) multiplier_11 (.a(in_1), .b(32'h40000), .out(multiplier_11_out));  // open: cin, cout
  Multiplier #(.width(32)) multiplier_12 (.a(in_1), .b(32'h20000), .out(multiplier_12_out));  // open: cin, cout
  Multiplier #(.width(32)) multiplier_13 (.a(in_1), .b(32'h10000), .out(multiplier_13_out));  // open: cin, cout
  Multiplier #(.width(32)) multiplier_14 (.a(in_1), .b(32'h8000), .out(multiplier_14_out));  // open: cin, cout
  Multiplier #(.width(32)) multiplier_15 (.a(in_1), .b(32'h4000), .out(multiplier_15_out));  // open: cin, cout
  Multiplier #(.width(32)) multiplier_16 (.a(in_1), .b(32'h2000), .out(multiplier_16_out));  // open: cin, cout
  or or_1 (or_1_out, in_5, in_2);
  Counter #(.width(5), .max('h1f)) counter_1 (
    .load(or_1_out), .D(5'b00101), .count(not_1_out), .Q(counter_1_q), .clk(ckolk), .clr(in_3));  // open: carry
  not not_1 (not_1_out, in_5);
  Multiplexer #(.select(4), .width(32), .enable("false")) multiplexer_1 (
    .in0(multiplier_1_out), .in1(multiplier_2_out), .in2(multiplier_3_out), .in3(multiplier_4_out),
    .in4(multiplier_5_out), .in5(multiplier_6_out), .in6(multiplier_7_out), .in7(multiplier_8_out),
    .in8(multiplier_9_out), .in9(multiplier_10_out), .in10(multiplier_11_out), .in11(multiplier_12_out),
    .in12(multiplier_13_out), .in13(multiplier_14_out), .in14(multiplier_15_out), .in15(multiplier_16_out),
    .out(out_6), .sel(bit_extender_1_out));
  Bit_Extender #(.in_width(5), .out_width(4)) bit_extender_1 (.in(counter_1_q), .out(bit_extender_1_out));
  Comparator #(.width(5)) comparator_1 (.a(counter_1_q), .b({5{1'b0}}), .eq(comparator_1_eq));  // open: gt, lt
  Comparator #(.width(5)) comparator_2 (.a(counter_1_q), .b(5'b01111), .lt(comparator_2_lt));  // open: gt, eq
  and and_1 (and_1_out, in_4, comparator_2_lt);
  and and_2 (and_2_out, or_1_out, in_4);
  and and_3 (and_3_out, comparator_1_eq, or_1_out);
  not not_2 (not_2_out, and_3_out);
  or or_2 (or_2_out, and_1_out, and_2_out);
  and and_4 (and_4_out, not_2_out, or_2_out);
  or or_3 (ckolk, and_4_out, in_5);

  // Other names for the same wires on the sheet: start = in_5
endmodule

module _3 (
  input  [31:0] in_1,
  input  [31:0] in_2,
  input  [31:0] in_3,
  input  [31:0] in_4,
  input  [31:0] in_5,
  input  in_6,
  input  in_7,
  input  in_8,
  input  in_9,
  output [31:0] out_10,
  output [31:0] out_11,
  output [31:0] out_12,
  output [31:0] out_13,
  output [31:0] out_14,
  output [31:0] out_15,
  output [31:0] out_16,
  output [31:0] out_17,
  output [31:0] out_18,
  output [31:0] out_19,
  output [31:0] out_20,
  output [31:0] out_21,
  output [31:0] out_22,
  output [31:0] out_23,
  output [31:0] out_24
);

  wire and_1_out, and_2_out, and_3_out, and_4_out, comparator_1_eq, comparator_2_lt, not_1_out, not_2_out,
       or_1_out, or_2_out, or_3_out;
  wire [3:0] bit_extender_1_out;
  wire [4:0] counter_1_q;

  or or_1 (or_1_out, in_9, in_6);
  not not_1 (not_1_out, in_9);
  or or_2 (or_2_out, and_1_out, in_9);
  Counter #(.width(5), .max('h1f)) counter_1 (
    .load(or_1_out), .D(5'b00101), .count(not_1_out), .Q(counter_1_q), .clk(or_2_out), .clr(in_7));  // open: carry
  and and_1 (and_1_out, not_2_out, or_3_out);
  or or_3 (or_3_out, and_4_out, and_3_out);
  Comparator #(.width(5)) comparator_1 (.a(counter_1_q), .b({5{1'b0}}), .eq(comparator_1_eq));  // open: gt, lt
  Comparator #(.width(5)) comparator_2 (.a(counter_1_q), .b(5'b01010), .lt(comparator_2_lt));  // open: gt, eq
  Multiplexer #(.select(4), .width(32), .enable("false")) multiplexer_1 (
    .in0(in_1), .in1({32{1'b0}}), .in2({32{1'b0}}), .in3({32{1'b0}}), .in4({32{1'b0}}), .in5({32{1'b0}}),
    .in6({32{1'b0}}), .in7({32{1'b0}}), .in8({32{1'b0}}), .in9({32{1'b0}}), .in10({32{1'b0}}),
    .in11({32{1'b0}}), .in12({32{1'b0}}), .in13({32{1'b0}}), .in14({32{1'b0}}), .in15({32{1'b0}}),
    .out(out_10), .sel(bit_extender_1_out));
  Multiplexer #(.select(4), .width(32), .enable("false")) multiplexer_2 (
    .in0(in_2), .in1(in_1), .in2({32{1'b0}}), .in3({32{1'b0}}), .in4({32{1'b0}}), .in5({32{1'b0}}),
    .in6({32{1'b0}}), .in7({32{1'b0}}), .in8({32{1'b0}}), .in9({32{1'b0}}), .in10({32{1'b0}}),
    .in11({32{1'b0}}), .in12({32{1'b0}}), .in13({32{1'b0}}), .in14({32{1'b0}}), .in15({32{1'b0}}),
    .out(out_11), .sel(bit_extender_1_out));
  Multiplexer #(.select(4), .width(32), .enable("false")) multiplexer_3 (
    .in0(in_3), .in1(in_2), .in2(in_1), .in3({32{1'b0}}), .in4({32{1'b0}}), .in5({32{1'b0}}),
    .in6({32{1'b0}}), .in7({32{1'b0}}), .in8({32{1'b0}}), .in9({32{1'b0}}), .in10({32{1'b0}}),
    .in11({32{1'b0}}), .in12({32{1'b0}}), .in13({32{1'b0}}), .in14({32{1'b0}}), .in15({32{1'b0}}),
    .out(out_12), .sel(bit_extender_1_out));
  Multiplexer #(.select(4), .width(32), .enable("false")) multiplexer_4 (
    .in0(in_4), .in1(in_3), .in2(in_2), .in3(in_1), .in4({32{1'b0}}), .in5({32{1'b0}}), .in6({32{1'b0}}),
    .in7({32{1'b0}}), .in8({32{1'b0}}), .in9({32{1'b0}}), .in10({32{1'b0}}), .in11({32{1'b0}}),
    .in12({32{1'b0}}), .in13({32{1'b0}}), .in14({32{1'b0}}), .in15({32{1'b0}}), .out(out_13),
    .sel(bit_extender_1_out));
  Multiplexer #(.select(4), .width(32), .enable("false")) multiplexer_5 (
    .in0(in_5), .in1(in_4), .in2(in_3), .in3(in_2), .in4(in_1), .in5({32{1'b0}}), .in6({32{1'b0}}),
    .in7({32{1'b0}}), .in8({32{1'b0}}), .in9({32{1'b0}}), .in10({32{1'b0}}), .in11({32{1'b0}}),
    .in12({32{1'b0}}), .in13({32{1'b0}}), .in14({32{1'b0}}), .in15({32{1'b0}}), .out(out_14),
    .sel(bit_extender_1_out));
  Multiplexer #(.select(4), .width(32), .enable("false")) multiplexer_6 (
    .in0({32{1'b0}}), .in1(in_5), .in2(in_4), .in3(in_3), .in4(in_2), .in5(in_1), .in6({32{1'b0}}),
    .in7({32{1'b0}}), .in8({32{1'b0}}), .in9({32{1'b0}}), .in10({32{1'b0}}), .in11({32{1'b0}}),
    .in12({32{1'b0}}), .in13({32{1'b0}}), .in14({32{1'b0}}), .in15({32{1'b0}}), .out(out_15),
    .sel(bit_extender_1_out));
  Multiplexer #(.select(4), .width(32), .enable("false")) multiplexer_7 (
    .in0({32{1'b0}}), .in1({32{1'b0}}), .in2(in_5), .in3(in_4), .in4(in_3), .in5(in_2), .in6(in_1),
    .in7({32{1'b0}}), .in8({32{1'b0}}), .in9({32{1'b0}}), .in10({32{1'b0}}), .in11({32{1'b0}}),
    .in12({32{1'b0}}), .in13({32{1'b0}}), .in14({32{1'b0}}), .in15({32{1'b0}}), .out(out_16),
    .sel(bit_extender_1_out));
  Multiplexer #(.select(4), .width(32), .enable("false")) multiplexer_8 (
    .in0({32{1'b0}}), .in1({32{1'b0}}), .in2({32{1'b0}}), .in3(in_5), .in4(in_4), .in5(in_3), .in6(in_2),
    .in7(in_1), .in8({32{1'b0}}), .in9({32{1'b0}}), .in10({32{1'b0}}), .in11({32{1'b0}}), .in12({32{1'b0}}),
    .in13({32{1'b0}}), .in14({32{1'b0}}), .in15({32{1'b0}}), .out(out_17), .sel(bit_extender_1_out));
  Multiplexer #(.select(4), .width(32), .enable("false")) multiplexer_9 (
    .in0({32{1'b0}}), .in1({32{1'b0}}), .in2({32{1'b0}}), .in3({32{1'b0}}), .in4(in_5), .in5(in_4),
    .in6(in_3), .in7(in_2), .in8(in_1), .in9({32{1'b0}}), .in10({32{1'b0}}), .in11({32{1'b0}}),
    .in12({32{1'b0}}), .in13({32{1'b0}}), .in14({32{1'b0}}), .in15({32{1'b0}}), .out(out_18),
    .sel(bit_extender_1_out));
  Multiplexer #(.select(4), .width(32), .enable("false")) multiplexer_10 (
    .in0({32{1'b0}}), .in1({32{1'b0}}), .in2({32{1'b0}}), .in3({32{1'b0}}), .in4({32{1'b0}}), .in5(in_5),
    .in6(in_4), .in7(in_3), .in8(in_2), .in9(in_1), .in10({32{1'b0}}), .in11({32{1'b0}}), .in12({32{1'b0}}),
    .in13({32{1'b0}}), .in14({32{1'b0}}), .in15({32{1'b0}}), .out(out_19), .sel(bit_extender_1_out));
  Multiplexer #(.select(4), .width(32), .enable("false")) multiplexer_11 (
    .in0({32{1'b0}}), .in1({32{1'b0}}), .in2({32{1'b0}}), .in3({32{1'b0}}), .in4({32{1'b0}}),
    .in5({32{1'b0}}), .in6(in_5), .in7(in_4), .in8(in_3), .in9(in_2), .in10(in_1), .in11({32{1'b0}}),
    .in12({32{1'b0}}), .in13({32{1'b0}}), .in14({32{1'b0}}), .in15({32{1'b0}}), .out(out_20),
    .sel(bit_extender_1_out));
  Multiplexer #(.select(4), .width(32), .enable("false")) multiplexer_12 (
    .in0({32{1'b0}}), .in1({32{1'b0}}), .in2({32{1'b0}}), .in3({32{1'b0}}), .in4({32{1'b0}}),
    .in5({32{1'b0}}), .in6({32{1'b0}}), .in7(in_5), .in8(in_4), .in9(in_3), .in10(in_2), .in11(in_1),
    .in12({32{1'b0}}), .in13({32{1'b0}}), .in14({32{1'b0}}), .in15({32{1'b0}}), .out(out_21),
    .sel(bit_extender_1_out));
  Multiplexer #(.select(4), .width(32), .enable("false")) multiplexer_13 (
    .in0({32{1'b0}}), .in1({32{1'b0}}), .in2({32{1'b0}}), .in3({32{1'b0}}), .in4({32{1'b0}}),
    .in5({32{1'b0}}), .in6({32{1'b0}}), .in7({32{1'b0}}), .in8(in_5), .in9(in_4), .in10(in_3), .in11(in_2),
    .in12(in_1), .in13({32{1'b0}}), .in14({32{1'b0}}), .in15({32{1'b0}}), .out(out_22),
    .sel(bit_extender_1_out));
  Multiplexer #(.select(4), .width(32), .enable("false")) multiplexer_14 (
    .in0({32{1'b0}}), .in1({32{1'b0}}), .in2({32{1'b0}}), .in3({32{1'b0}}), .in4({32{1'b0}}),
    .in5({32{1'b0}}), .in6({32{1'b0}}), .in7({32{1'b0}}), .in8({32{1'b0}}), .in9(in_5), .in10(in_4),
    .in11(in_3), .in12(in_2), .in13(in_1), .in14({32{1'b0}}), .in15({32{1'b0}}), .out(out_23),
    .sel(bit_extender_1_out));
  Multiplexer #(.select(4), .width(32), .enable("false")) multiplexer_15 (
    .in0({32{1'b0}}), .in1({32{1'b0}}), .in2({32{1'b0}}), .in3({32{1'b0}}), .in4({32{1'b0}}),
    .in5({32{1'b0}}), .in6({32{1'b0}}), .in7({32{1'b0}}), .in8({32{1'b0}}), .in9({32{1'b0}}), .in10(in_5),
    .in11(in_4), .in12(in_3), .in13(in_2), .in14(in_1), .in15({32{1'b0}}), .out(out_24),
    .sel(bit_extender_1_out));
  Bit_Extender #(.in_width(5), .out_width(4)) bit_extender_1 (.in(counter_1_q), .out(bit_extender_1_out));
  and and_2 (and_2_out, comparator_1_eq, or_1_out);
  and and_3 (and_3_out, comparator_2_lt, in_8);
  and and_4 (and_4_out, in_8, or_1_out);
  not not_2 (not_2_out, and_2_out);

  // Other names for the same wires on the sheet: _1[31:0] = in_1; _2[31:0] = in_2; _3[31:0] = in_3; _4[31:0] = in_4;
  //   _5[31:0] = in_5; start = in_9
endmodule
